// Logisim project Project1Given.circ as structural Verilog: 4 circuits, main circuit main
module main (
  input  in_1,
  input  in_2,
  input  in_3,
  input  in_4,
  input  Five,
  output N,
  output E,
  output [3:0] out_8
);

  wire fiveseven_1_a, fiveseven_1_b, fiveseven_1_c, fiveseven_1_d, fiveseven_1_e, fiveseven_1_f,
       fiveseven_1_g;

  Compare compare_1 (.X0(1'b1), .X1(1'b0), .X2(1'b1), .Y0(1'b1), .Y1(1'b0), .Y2(1'b1), .N(N), .E(E));
  Gray gray_1 (.B0(1'b1), .B1(1'b1), .B2(1'b0), .B3(1'b1), .G0(out_8[0]), .G1(out_8[1]), .G2(out_8[2]), .G3(out_8[3]));
  FiveSeven fiveseven_1 (
    .V(in_1), .W(in_2), .X(in_3), .Y(in_4), .Z(Five), .A(fiveseven_1_a), .B(fiveseven_1_b),
    .C(fiveseven_1_c), .D(fiveseven_1_d), .E(fiveseven_1_e), .F(fiveseven_1_f), .G(fiveseven_1_g));
  _7_Segment_Display u_7_segment_display_1 (
    .g(fiveseven_1_g), .f(fiveseven_1_f), .a(fiveseven_1_a), .b(fiveseven_1_b), .e(fiveseven_1_e),
    .d(fiveseven_1_d), .c(fiveseven_1_c));  // open: dp
endmodule

module Compare (
  input  X0,
  input  X1,
  input  X2,
  input  Y0,
  input  Y1,
  input  Y2,
  output N,
  output E
);

  wire eq0_out, eq1_out, eq2_out, It0_out, It1_out, It2_out, not_1_out, not_2_out, not_3_out, not_4_out,
       not_5_out, t1_out, t2_out;

  not not_1 (not_1_out, X0);
  not not_2 (not_2_out, X1);
  not not_3 (not_3_out, X2);
  xor eq1 (eq1_out, X1, Y1);
  xor eq2 (eq2_out, X2, Y2);
  and It0 (It0_out, not_1_out, Y0);
  and It1 (It1_out, not_2_out, Y1);
  and It2 (It2_out, not_3_out, Y2);
  xor eq0 (eq0_out, X0, Y0);
  not not_4 (not_4_out, eq0_out);
  not not_5 (not_5_out, eq1_out);
  not not_6 (not_4_out, eq2_out);
  and t1 (t1_out, It1_out, not_4_out);
  and t2 (t2_out, not_4_out, It0_out);
  or or_1 (N, t1_out, t2_out, It2_out);
  and and_1 (E, not_4_out, not_5_out, not_4_out);
endmodule

module Gray (
  input  B0,
  input  B1,
  input  B2,
  input  B3,
  output G0,
  output G1,
  output G2,
  output G3
);

  wire m0_out, m1_out, m2_out, m3_out, m4_out, m5_out, m6_out, m7_out, m8_out, m9_out, m10_out, m11_out,
       m12_out, m13_out, m14_out, m15_out, not_1_out, not_2_out, not_3_out, not_4_out;

  not not_1 (not_1_out, B0);
  not not_2 (not_2_out, B1);
  not not_3 (not_3_out, B2);
  not not_4 (not_4_out, B3);
  and m0 (m0_out, not_1_out, not_2_out, not_3_out, not_4_out);
  and m1 (m1_out, B0, not_2_out, not_3_out, not_4_out);
  and m2 (m2_out, not_4_out, B1, not_3_out, not_4_out);
  and m3 (m3_out, B0, B1, not_3_out, not_4_out);
  and m4 (m4_out, not_1_out, not_2_out, B2, not_4_out);
  and m5 (m5_out, B0, not_2_out, B2, not_4_out);
  and m6 (m6_out, not_1_out, B1, B2, not_4_out);
  and m7 (m7_out, B0, B1, B2, not_4_out);
  and m8 (m8_out, not_1_out, not_2_out, not_3_out, B3);
  and m9 (m9_out, B0, not_2_out, not_3_out, B3);
  and m10 (m10_out, not_1_out, B1, not_3_out, B3);
  and m11 (m11_out, B0, B1, not_3_out, B3);
  and m12 (m12_out, not_1_out, not_2_out, B2, B3);
  and m13 (m13_out, B0, not_2_out, B2, B3);
  and m14 (m14_out, not_1_out, B1, B2, B3);
  and m15 (m15_out, B0, B1, B2, B3);
  or g00 (G0, m0_out, m1_out, m4_out, m5_out, m8_out, m9_out, m12_out, m13_out);
  or g01 (G1, m0_out, m5_out, m6_out, m7_out, m8_out, m13_out, m14_out, m15_out);
  or g02 (G2, m0_out, m1_out, m2_out, m3_out, m4_out, m5_out, m6_out, m15_out);
  or g03 (G3, m3_out, m4_out, m5_out, m6_out, m7_out, m8_out, m9_out, m10_out);
endmodule

module FiveSeven (
  input  V,
  input  W,
  input  X,
  input  Y,
  input  Z,
  output A,
  output B,
  output C,
  output D,
  output E,
  output F,
  output G
);

  wire D0_out, D1_out, D2_out, D3_out, D4_out, D5_out, D6_out, D7_out, D8_out, D9_out, k0_out, k1_out,
       k2_out, k3_out, k4_out, k11_out, k12_out, k13_out, k14_out, k21_out, k22_out, k23_out, k24_out,
       k25_out, k26_out, k31_out, k32_out, k33_out, k34_out, not_1_out, not_2_out, not_3_out, not_4_out,
       not_5_out;

  not not_1 (not_1_out, V);
  not not_2 (not_2_out, W);
  not not_3 (not_3_out, X);
  not not_4 (not_4_out, Y);
  not not_5 (not_5_out, Z);
  and k11 (k11_out, V, not_2_out, not_3_out, not_4_out);
  and k12 (k12_out, not_1_out, W, not_3_out, not_4_out);
  and k13 (k13_out, not_1_out, not_2_out, X, not_4_out);
  and k14 (k14_out, not_1_out, not_2_out, not_3_out, Y);
  and k21 (k21_out, V, W, not_3_out, not_4_out);
  and k22 (k22_out, V, not_2_out, X, not_4_out);
  and k23 (k23_out, V, not_2_out, not_3_out, Y);
  and k24 (k24_out, not_1_out, W, X, not_4_out);
  and k25 (k25_out, not_1_out, W, not_3_out, Y);
  and k26 (k26_out, not_1_out, not_2_out, X, Y);
  and k31 (k31_out, not_1_out, W, X, Y);
  and k32 (k32_out, V, not_2_out, X, Y);
  and k33 (k33_out, V, W, not_3_out, Y);
  and k34 (k34_out, V, W, X, not_4_out);
  and k0 (k0_out, not_1_out, not_2_out, not_3_out, not_4_out);
  and k4 (k4_out, V, W, X, Y);
  or k1 (k1_out, k11_out, k12_out, k13_out, k14_out);
  or k2 (k2_out, k21_out, k22_out, k23_out, k24_out, k25_out, k26_out);
  and D6 (D6_out, k1_out, Z);
  or k3 (k3_out, k31_out, k32_out, k33_out, k34_out);
  and D8 (D8_out, k3_out, Z);
  and D1 (D1_out, k1_out, not_5_out);
  and D7 (D7_out, k2_out, Z);
  and D3 (D3_out, k3_out, not_5_out);
  and D0 (D0_out, k0_out, not_5_out);
  and D4 (D4_out, k4_out, not_5_out);
  and D2 (D2_out, not_5_out, k2_out);
  and D5 (D5_out, k0_out, Z);
  and D9 (D9_out, k4_out, Z);
  or a00 (A, D0_out, D2_out, D3_out, D5_out, D6_out, D7_out, D8_out, D9_out);
  or b00 (B, D0_out, D1_out, D2_out, D3_out, D4_out, D7_out, D8_out, D9_out);
  or c00 (C, D0_out, D1_out, D3_out, D4_out, D5_out, D6_out, D7_out, D8_out, D9_out);
  or d00 (D, D0_out, D2_out, D3_out, D5_out, D6_out, D8_out, D9_out);
  or e00 (E, D0_out, D2_out, D6_out, D8_out);
  or f00 (F, D0_out, D4_out, D5_out, D6_out, D8_out, D9_out);
  or g00 (G, D2_out, D3_out, D4_out, D5_out, D6_out, D8_out, D9_out);
endmodule
